# Fritzing sketch realPong (saved by Fritzing 0.9.5d)
breadboards: 1

parts:
  Parça1 = Arduino Uno (Rev3)
  R1 = Rotary Potentiometer (Small) [maximum_resistance=100kΩ package=THT]
  R2 = Rotary Potentiometer (Small) [maximum_resistance=100kΩ package=THT]

nets:
  N1: Parça1.A1, R1.wiper
  N2: Parça1.A2, R2.wiper
  N3: Parça1.GND, R1.leg2, R2.leg2
  N4: Parça1.5V, R1.leg1, R2.leg1
