# Fritzing sketch pongController (saved by Fritzing 0.9.5d)
breadboards: 1

parts:
  R1 = Rotary Potentiometer (Small) [maximum_resistance=100kΩ package=THT]
  Parça1 = Arduino Uno (Rev3)

nets:
  N1: R1.leg1, Parça1.5V
  N2: R1.wiper, Parça1.A1
  N3: R1.leg2, Parça1.GND
